# Fritzing sketch rasunho (saved by Fritzing 0.9.4)
circuit board: 6.2cm x 8.0501cm

parts:
  Teensy_LC1 = Teensy-LC
  GY1 = GY-521 (MPU-6050) [form="♀ (female)" package=THT]
  BMP280 = BMP280 Breakout Board [part_number=BMP280]
  microSD1 = MicroSD Card Module
  J1 = Basic Servo
  J2 = Basic Servo
  LED1 = LED - 5mm [color="Red (633nm)" package="5 mm [THT]"]
  LED2 = LED - 5mm [color="Red (633nm)" package="5 mm [THT]"]

nets:
  GND: Teensy_LC1.GND, microSD1.GND, J1.gnd, J2.gnd, LED1.anode, LED2.anode
  N1: Teensy_LC1.D5, LED1.cathode
  N2: Teensy_LC1.D6, LED2.cathode
  N3: Teensy_LC1.D9, J2.pulse
  N4: Teensy_LC1.D10, J1.pulse
  N5: Teensy_LC1.A4/D18, GY1.pin4, BMP280.SDA
  N6: Teensy_LC1.A5/D19, GY1.pin3, BMP280.SCL
  3V3: Teensy_LC1.3V3, GY1.pin1, BMP280.VCC
  N7: Teensy_LC1.AGND, GY1.pin2, BMP280.GND
  VCC: Teensy_LC1.Vin, microSD1.VCC, J1.vcc, J2.vcc

custom parts:
  Teensy-LC: Teensy-LC (Low Cost) is a powerful 32 bit microcontroller board, with a rich set of hardware peripherals, at a very affordable price! Teensy-LC delivers an impressive collection of capabilities to make modern electronic projects simpler. It features an ARM Cortex-M0+ processor at 48 MHz, 62K Flash, 8K RAM, 12 bit analog input & output, hardware Serial, SPI & I2C, USB, and a total of 27 I/O pins.
  GY-521 (MPU-6050): Placa GY-521 basada en conjunto de acelerómetro+giroscopios MPU-6050
  BMP280 Breakout Board: This is a breakout board for the Bosch Sensortec BMP280, "an absolute barometric pressure sensor especially designed for mobile applications." The operation range is 300 to 1100 hPa. Supply voltage is 1.2 to 3.6V. Operating temperature range is -40 to +85 °C.
